// Digital circuit cpu.dig as structural Verilog
module cpu (
  input  clock,
  input  in_2,
  input  in_11,
  input  in_12,
  output [7:0] A_register,
  output [7:0] B_register,
  output [7:0] Mem_addr_register,
  output [7:0] RAM,
  output [7:0] ALU,
  output [7:0] Instruction_register,
  output [7:0] Output,
  output [7:0] Program_counter
);

  wire AI, and_1_out, and_3_out, AO, BI, CE, CLK, CO, counterpreset_1_ovf, EO, FI, HT, II, J, MAI,
       multiplexer_1_out, not_1_out, not_2_out, OI, or_1_out, or_2_out, RI, RO, SU, T0;
  wire [1:0] add_1_c_o, FLAGS;
  wire [7:0] multiplexer_2_out, xor_1_out;
  wire [10:8] TCLK_out;

  or or_1 (or_1_out, T0, in_2);
  Multiplexer multiplexer_1 (.sel(in_12), .in_0(in_11), .in_1(clock), .out(multiplexer_1_out));
  and and_1 (and_1_out, not_1_out, and_3_out);
  not not_1 (not_1_out, TCLK_out[9]);
  or or_2 (or_2_out, or_1_out, and_1_out);
  and and_2 (CLK, multiplexer_1_out, ~HT);  // And
  Register #(.Bits(8)) MAR (.D(RAM), .C(CLK), .en(MAI), .Q(Mem_addr_register));
  RAMSinglePort #(.AddrBits(8), .isProgramMemory("true"), .Bits(8)) ramsingleport_1 (
    .A(Mem_addr_register), .str(RI), .C(CLK), .ld(RO), .D(RAM));
  Register #(.Bits(8)) Out_reg (.D(RAM), .C(CLK), .en(OI), .Q(Output));
  Register #(.Bits(8)) Instr_reg (.D(RAM), .C(CLK), .en(II), .Q(Instruction_register));
  CounterPreset #(.Bits(3), .isProgramCounter("true")) TCLK (
    .en(1'b1), .C(not_2_out), .dir(1'b0), .in(3'b000), .ld(1'b0), .clr(or_2_out), .out(TCLK_out));  // open: ovf
  not not_2 (not_2_out, CLK);
  and and_3 (and_3_out, TCLK_out[10], TCLK_out[8]);
  ROM #(.AddrBits(13), .Bits(16)) UCODE (
    .A({FLAGS, TCLK_out, Instruction_register}), .sel(1'b1),
    .D({CO, CE, J, AI, AO, BI, EO, SU, MAI, RI, RO, II, OI, HT, T0, FI}));
  assign RAM = EO ? ALU : 8'bz;  // Driver driver_1
  assign RAM = CO ? Program_counter : 8'bz;  // Driver driver_2
  CounterPreset #(.Bits(8), .isProgramCounter("true")) counterpreset_1 (
    .en(CE), .C(CLK), .dir(1'b0), .in(RAM), .ld(J), .clr(in_2), .out(Program_counter),
    .ovf(counterpreset_1_ovf));
  assign RAM = AO ? A_register : 8'bz;  // Driver driver_3
  Register #(.Bits(8)) register_1 (.D(RAM), .C(CLK), .en(AI), .Q(A_register));
  Register #(.Bits(2)) Flags_reg (.D(add_1_c_o), .C(CLK), .en(FI), .Q(FLAGS));
  Register #(.Bits(8)) register_2 (.D(RAM), .C(CLK), .en(BI), .Q(B_register));
  LED led_1 (.in(counterpreset_1_ovf));
  Add #(.Bits(8)) add_1 (.a(A_register), .b(xor_1_out), .c_i(SU), .s(ALU), .c_o(add_1_c_o[0]));
  assign xor_1_out = B_register ^ multiplexer_2_out;  // XOr xor_1, 8 bits wide
  Multiplexer #(.Bits(8)) multiplexer_2 (.sel(SU), .in_0({8{1'b0}}), .in_1({8{1'b1}}), .out(multiplexer_2_out));
  nor nor_1 (add_1_c_o[1], ALU[0], ALU[1], ALU[2], ALU[3], ALU[4], ALU[5], ALU[6], ALU[7]);

  // Other names for the same wires on the sheet: a[7:0] = A_register; b[7:0] = B_register;
  //   ir[7:0] = Instruction_register; mar[7:0] = Mem_addr_register; out[7:0] = Output; pc[7:0] = Program_counter;
  //   RESET = in_2

  // Notes on the sheet:
  //   clock: Hz: 100
  //   T-Clock
  //   Control Logic
  //   Clock
  //   Memory Address Register
  //   RAM
  //   Output Register
  //   Instruction Register
  //   If TCLK=5
  //   UCODE loads ucode.hex
  //   Program Counter
  //   A Register
  //   Flags Register
  //   B Register
endmodule
